// Logisim project QZX_Adder.circ as structural Verilog
module half_adder (
  input  bit_0,
  input  bit_1,
  output carry,
  output sum
);

  and and_1 (carry, bit_0, bit_1);
  xor xor_1 (sum, bit_0, bit_1);
endmodule

module full_adder (
  input  carry_in,
  input  bit_1,
  input  bit_0,
  output carry_out,
  output sum
);

  wire half_adder_1_carry, half_adder_1_sum, half_adder_2_carry;

  half_adder half_adder_1 (.bit_0(carry_in), .bit_1(bit_1), .carry(half_adder_1_carry), .sum(half_adder_1_sum));
  or or_1 (carry_out, half_adder_1_carry, half_adder_2_carry);
  half_adder half_adder_2 (.bit_0(half_adder_1_sum), .bit_1(bit_0), .carry(half_adder_2_carry), .sum(sum));
endmodule
