// Logisim project Subtracter.circ as structural Verilog: 3 circuits, main circuit main
module main (
  input  [3:0] A,
  input  [3:0] B
);
endmodule

module Full_Subtracter (
  input  bit_1,
  input  bit_0,
  input  borrow_in,
  output borrow_out,
  output diff
);

  wire half_subtracter_1_borrow, half_subtracter_1_diff, half_subtracter_2_borrow;

  Half_Subtracter half_subtracter_1 (
    .bit_1(bit_1), .bit_0(bit_0), .borrow(half_subtracter_1_borrow), .diff(half_subtracter_1_diff));
  Half_Subtracter half_subtracter_2 (
    .bit_1(half_subtracter_1_diff), .bit_0(borrow_in), .borrow(half_subtracter_2_borrow), .diff(diff));
  or or_1 (borrow_out, half_subtracter_1_borrow, half_subtracter_2_borrow);
endmodule

module Half_Subtracter (
  input  bit_1,
  input  bit_0,
  output borrow,
  output diff
);

  wire not_1_out;

  not not_1 (not_1_out, bit_1);
  and and_1 (borrow, not_1_out, bit_0);
  xor xor_1 (diff, bit_1, bit_0);
endmodule
