// Logisim project OwnROM.circ as structural Verilog
module Rom16x8 (
  input  [3:0] S,
  output [7:0] Q
);

  wire [7:0] demultiplexer_2_out0, demultiplexer_2_out1, demultiplexer_5_out0, demultiplexer_5_out1,
       demultiplexer_8_out0, demultiplexer_8_out1, demultiplexer_11_out0, demultiplexer_11_out1,
       demultiplexer_13_out0, demultiplexer_13_out1, demultiplexer_14_out0, demultiplexer_14_out1,
       demultiplexer_15_out0, demultiplexer_15_out1, register_1_q, register_2_q, register_3_q, register_4_q,
       register_5_q, register_6_q, register_7_q, register_8_q, register_9_q, register_10_q, register_11_q,
       register_12_q, register_13_q, register_14_q, register_15_q, register_16_q;

  Register register_1 (.Q(register_1_q));  // open: D, en, clk, clr
  Register register_2 (.Q(register_2_q));  // open: D, en, clk, clr
  Register register_3 (.Q(register_3_q));  // open: D, en, clk, clr
  Register register_4 (.Q(register_4_q));  // open: D, en, clk, clr
  Register register_5 (.Q(register_5_q));  // open: D, en, clk, clr
  Register register_6 (.Q(register_6_q));  // open: D, en, clk, clr
  Register register_7 (.Q(register_7_q));  // open: D, en, clk, clr
  Register register_8 (.Q(register_8_q));  // open: D, en, clk, clr
  Register register_9 (.Q(register_9_q));  // open: D, en, clk, clr
  Register register_10 (.Q(register_10_q));  // open: D, en, clk, clr
  Register register_11 (.Q(register_11_q));  // open: D, en, clk, clr
  Register register_12 (.Q(register_12_q));  // open: D, en, clk, clr
  Register register_13 (.Q(register_13_q));  // open: D, en, clk, clr
  Register register_14 (.Q(register_14_q));  // open: D, en, clk, clr
  Register register_15 (.Q(register_15_q));  // open: D, en, clk, clr
  Register register_16 (.Q(register_16_q));  // open: D, en, clk, clr
  Demultiplexer #(.width(8)) demultiplexer_1 (
    .out0(register_1_q), .out1(register_2_q), .in(demultiplexer_2_out0), .sel(S[0]));
  Demultiplexer #(.width(8)) demultiplexer_2 (
    .out0(demultiplexer_2_out0), .out1(demultiplexer_2_out1), .in(demultiplexer_13_out0), .sel(S[1]));
  Demultiplexer #(.width(8)) demultiplexer_3 (
    .out0(register_3_q), .out1(register_4_q), .in(demultiplexer_2_out1), .sel(S[0]));
  Demultiplexer #(.width(8)) demultiplexer_4 (
    .out0(register_5_q), .out1(register_6_q), .in(demultiplexer_5_out0), .sel(S[0]));
  Demultiplexer #(.width(8)) demultiplexer_5 (
    .out0(demultiplexer_5_out0), .out1(demultiplexer_5_out1), .in(demultiplexer_13_out1), .sel(S[1]));
  Demultiplexer #(.width(8)) demultiplexer_6 (
    .out0(register_7_q), .out1(register_8_q), .in(demultiplexer_5_out1), .sel(S[0]));
  Demultiplexer #(.width(8)) demultiplexer_7 (
    .out0(register_9_q), .out1(register_10_q), .in(demultiplexer_8_out0), .sel(S[0]));
  Demultiplexer #(.width(8)) demultiplexer_8 (
    .out0(demultiplexer_8_out0), .out1(demultiplexer_8_out1), .in(demultiplexer_14_out0), .sel(S[1]));
  Demultiplexer #(.width(8)) demultiplexer_9 (
    .out0(register_11_q), .out1(register_12_q), .in(demultiplexer_8_out1), .sel(S[0]));
  Demultiplexer #(.width(8)) demultiplexer_10 (
    .out0(register_13_q), .out1(register_14_q), .in(demultiplexer_11_out0), .sel(S[0]));
  Demultiplexer #(.width(8)) demultiplexer_11 (
    .out0(demultiplexer_11_out0), .out1(demultiplexer_11_out1), .in(demultiplexer_14_out1), .sel(S[1]));
  Demultiplexer #(.width(8)) demultiplexer_12 (
    .out0(register_15_q), .out1(register_16_q), .in(demultiplexer_11_out1), .sel(S[0]));
  Demultiplexer #(.width(8)) demultiplexer_13 (
    .out0(demultiplexer_13_out0), .out1(demultiplexer_13_out1), .in(demultiplexer_15_out0), .sel(S[2]));
  Demultiplexer #(.width(8)) demultiplexer_14 (
    .out0(demultiplexer_14_out0), .out1(demultiplexer_14_out1), .in(demultiplexer_15_out1), .sel(S[2]));
  Demultiplexer #(.width(8)) demultiplexer_15 (
    .out0(demultiplexer_15_out0), .out1(demultiplexer_15_out1), .in(Q), .sel(S[3]));

  // Other names for the same wires on the sheet: S_0 = S[0]; S_1 = S[1]; S_2 = S[2]; S_3 = S[3]
endmodule

module RAM2x8 (
  input  [7:0] D,
  input  addr_0,
  input  addr_1,
  input  enable,
  input  reset,
  input  clock,
  output [7:0] Q
);

  wire [7:0] demultiplexer_2_out0, demultiplexer_2_out1, register_1_q, register_2_q, register_3_q,
       register_4_q;

  Register register_1 (.D(D), .en(enable), .clk(clock), .Q(register_1_q), .clr(reset));
  Register register_2 (.D(D), .en(enable), .clk(clock), .Q(register_2_q), .clr(reset));
  Register register_3 (.D(D), .en(enable), .clk(clock), .Q(register_3_q), .clr(reset));
  Register register_4 (.D(D), .en(enable), .clk(clock), .Q(register_4_q), .clr(reset));
  Demultiplexer #(.width(8)) demultiplexer_1 (
    .out0(register_1_q), .out1(register_2_q), .in(demultiplexer_2_out0), .sel(addr_0));
  Demultiplexer #(.width(8)) demultiplexer_2 (
    .out0(demultiplexer_2_out0), .out1(demultiplexer_2_out1), .in(Q), .sel(addr_1));
  Demultiplexer #(.width(8)) demultiplexer_3 (
    .out0(register_3_q), .out1(register_4_q), .in(demultiplexer_2_out1), .sel(addr_0));

  // Other names for the same wires on the sheet: S_0 = addr_0; S_1 = addr_1
endmodule
