// Logisim project sCPU.circ as structural Verilog: 1 circuit, main circuit main
module main (
);

  wire and_1_out, and_2_out, and_3_out, and_4_out, clock_1_out, clock_2_out, comparator_1_gt,
       comparator_1_lt, decoder_1_out0, decoder_1_out1, decoder_1_out2, decoder_1_out3, op_add, op_bner0,
       op_li, or_2_out, PC_load, rd_can_write, reset;
  wire [3:0] add_result, addr, r0_data, R1_q, R2_q, R3_q, rs1_data, rs2_data, write_data;
  wire [7:0] CMD, PC;

  // Probe on addr
  Button button_1 (.out(reset));
  Decoder #(.select(2)) decoder_1 (
    .out0(decoder_1_out0), .out1(decoder_1_out1), .out2(decoder_1_out2), .out3(decoder_1_out3),
    .sel(addr[3:2]));  // open: en
  Counter counter_1 (
    .clr(reset), .load(PC_load), .clk(clock_1_out), .D({4'b0000, addr}), .Q(PC));  // open: up, count, carry
  Clock clock_1 (.out(clock_1_out));
  // Probe on write_data
  Clock clock_2 (.out(clock_2_out));
  // Probe on PC
  Register #(.width(4)) R0 (.D(write_data), .en(and_1_out), .clk(clock_2_out), .Q(r0_data), .clr(reset));
  and and_1 (and_1_out, decoder_1_out0, rd_can_write);
  Register #(.width(4)) R1 (.D(write_data), .en(and_2_out), .clk(clock_2_out), .Q(R1_q), .clr(reset));
  and and_2 (and_2_out, decoder_1_out1, rd_can_write);
  Register #(.width(4)) R2 (.D(write_data), .en(and_3_out), .clk(clock_2_out), .Q(R2_q), .clr(reset));
  and and_3 (and_3_out, decoder_1_out2, rd_can_write);
  Register #(.trigger("falling"), .width(4)) R3 (
    .D(write_data), .en(and_4_out), .clk(clock_2_out), .Q(R3_q), .clr(reset));
  and and_4 (and_4_out, decoder_1_out3, rd_can_write);
  Decoder #(.select(2)) decoder_2 (.out0(op_add), .out2(op_li), .out3(op_bner0), .sel(CMD[7:6]));  // open: out1, en
  RAM #(.enables("line"), .trigger("high")) ram_1 (
    .addr(PC), .clk(1'b1), .dout({CMD[7:6], addr, CMD[1:0]}));  // open: we, din
  or or_1 (rd_can_write, op_add, op_li);
  Multiplexer #(.select(2), .width(4)) multiplexer_1 (
    .in0(add_result), .in2({addr[1:0], CMD[1:0]}), .out(write_data), .sel(CMD[7:6]));  // open: in1, in3
  Multiplexer #(.select(2), .width(4)) multiplexer_2 (
    .in0(r0_data), .in1(R1_q), .in2(R2_q), .in3(R3_q), .out(rs1_data), .sel(addr[1:0]));
  // Probe on rs1_data
  Multiplexer #(.select(2), .width(4)) multiplexer_3 (
    .in0(r0_data), .in1(R1_q), .in2(R2_q), .in3(R3_q), .out(rs2_data), .sel(CMD[1:0]));
  // Probe on rs2_data
  // Probe on {CMD[7:6], addr, CMD[1:0]}
  Adder #(.width(4)) adder_1 (.a(rs1_data), .b(rs2_data), .out(add_result));  // open: cin, cout
  Comparator #(.mode("unsigned"), .width(4)) comparator_1 (
    .a(r0_data), .b(rs2_data), .gt(comparator_1_gt), .lt(comparator_1_lt));  // open: eq
  or or_2 (or_2_out, comparator_1_gt, comparator_1_lt);
  and and_5 (PC_load, or_2_out, op_bner0);

  // Other names for the same wires on the sheet: CMD[5:2] = addr; rd[1:0] = addr[3:2];
  //   imm[3:0] = {addr[1:0], CMD[1:0]}; rs1[1:0] = addr[1:0]; op_code[1:0] = CMD[7:6]; rs2[1:0] = CMD[1:0]
endmodule
